# Fritzing sketch uPyMPU (saved by Fritzing 0.9.3b)

parts:
  PCB1 = Arduino Shield PCB  # not connected
  Part1 = WIPY 2.0/3.0 [part_number="wipy 3.0"]
  C2 = Capacitor Polarized [package=cpol-radial-100uf-25v]
  C1 = Capacitor Polarized [package=cpol-radial-100uf-25v]
  J1 = Basic Servo
  J2 = Basic Servo
  GY1 = MPU-6050 Board GY-521 [form="♀ (female)" package=THT]

nets:
  GND: Part1.GND, C2.-, C1.-, J1.gnd, J2.gnd, GY1.pin2
  N1: Part1.3V3, GY1.pin1
  N2: Part1.P3, J2.pulse
  N3: Part1.P7, J1.pulse
  N4: Part1.P9, GY1.pin4
  N5: Part1.P10, GY1.pin3
  N6: C2.+, J1.vcc
  N7: C1.+, J2.vcc

custom parts:
  Arduino Shield PCB: Plain PCB Shaped to fit an Arduino "Shield"
  MPU-6050 Board GY-521: Acelerometro y Giroscopio MPU-6050 Board GY-521
